// Logisim project 4bit_cpu.circ as structural Verilog
module L_4bit_Adder_fc6744fc (
  input  Cin,
  input  A0,
  input  B0,
  input  A1,
  input  B1,
  input  A2,
  input  B2,
  input  A3,
  input  B3,
  output F0,
  output F1,
  output F2,
  output F3,
  output Cout
);

  wire adder_1_cout, adder_2_cout, adder_3_cout;

  Adder #(.width(1)) adder_1 (.a(A0), .b(B0), .out(F0), .cin(Cin), .cout(adder_1_cout));
  Adder #(.width(1)) adder_2 (.a(A1), .b(B1), .out(F1), .cin(adder_1_cout), .cout(adder_2_cout));
  Adder #(.width(1)) adder_3 (.a(A2), .b(B2), .out(F2), .cin(adder_2_cout), .cout(adder_3_cout));
  Adder #(.width(1)) adder_4 (.a(A3), .b(B3), .out(F3), .cin(adder_3_cout), .cout(Cout));
endmodule

module L_4bit_Sub_beb1027c (
  input  B0,
  input  A0,
  input  B1,
  input  A1,
  input  A2,
  input  B2,
  input  A3,
  input  B3,
  output F0,
  output F1,
  output F2,
  output F3,
  output Cout
);

  wire adder_1_cout, adder_2_cout, adder_3_cout, xor_1_out, xor_2_out, xor_3_out, xor_4_out;

  xor xor_1 (xor_1_out, B1, 1'b1);
  xor xor_2 (xor_2_out, B2, 1'b1);
  xor xor_3 (xor_3_out, B3, 1'b1);
  xor xor_4 (xor_4_out, B0, 1'b1);
  Adder #(.width(1)) adder_1 (.a(A0), .b(xor_4_out), .out(F0), .cin(1'b1), .cout(adder_1_cout));
  Adder #(.width(1)) adder_2 (.a(A1), .b(xor_1_out), .out(F1), .cin(adder_1_cout), .cout(adder_2_cout));
  Adder #(.width(1)) adder_3 (.a(A2), .b(xor_2_out), .out(F2), .cin(adder_2_cout), .cout(adder_3_cout));
  Adder #(.width(1)) adder_4 (.a(A3), .b(xor_3_out), .out(F3), .cin(adder_3_cout), .cout(Cout));
endmodule

module L_4bit_AND_42e6373c (
  input  A0,
  input  B0,
  input  A1,
  input  B1,
  input  A2,
  input  B2,
  input  A3,
  input  B3,
  output F0,
  output F1,
  output F2,
  output F3
);

  and and_1 (F0, A0, B0);
  and and_2 (F1, A1, B1);
  and and_3 (F2, A2, B2);
  and and_4 (F3, A3, B3);
endmodule

module L_4bit_OR_4fc8127c (
  input  A0,
  input  B0,
  input  A1,
  input  B1,
  input  A2,
  input  B2,
  input  A3,
  input  B3,
  output F0,
  output F1,
  output F2,
  output F3
);

  or or_1 (F0, A0, B0);
  or or_2 (F1, A1, B1);
  or or_3 (F2, A2, B2);
  or or_4 (F3, A3, B3);
endmodule

module L_4bit_XOR_4aeb7194 (
  input  A0,
  input  B0,
  input  A1,
  input  B1,
  input  A2,
  input  B2,
  input  A3,
  input  B3,
  output F0,
  output F1,
  output F2,
  output F3
);

  xor xor_1 (F0, A0, B0);
  xor xor_2 (F1, A1, B1);
  xor xor_3 (F2, A2, B2);
  xor xor_4 (F3, A3, B3);
endmodule

module L_4bit_NOT_d5e80a42 (
  input  A0,
  input  A1,
  input  A2,
  input  A3,
  output F0,
  output F1,
  output F2,
  output F3
);

  not not_1 (F0, A0);
  not not_2 (F1, A1);
  not not_3 (F2, A2);
  not not_4 (F3, A3);
endmodule

module L_4bit_ALU_eb8587b2 (
  input  A0,
  input  B0,
  input  A1,
  input  B1,
  input  A2,
  input  B2,
  input  A3,
  input  B3,
  input  [2:0] Opcode,
  output F0,
  output F1,
  output F2,
  output F3,
  output Cout
);

  wire l_4bit_adder_fc6744fc_1_f0, l_4bit_adder_fc6744fc_1_f1, l_4bit_adder_fc6744fc_1_f2,
       l_4bit_adder_fc6744fc_1_f3, l_4bit_and_42e6373c_1_f0, l_4bit_and_42e6373c_1_f1,
       l_4bit_and_42e6373c_1_f2, l_4bit_and_42e6373c_1_f3, l_4bit_not_d5e80a42_1_f0,
       l_4bit_not_d5e80a42_1_f1, l_4bit_not_d5e80a42_1_f2, l_4bit_not_d5e80a42_1_f3, l_4bit_or_4fc8127c_1_f0,
       l_4bit_or_4fc8127c_1_f1, l_4bit_or_4fc8127c_1_f2, l_4bit_or_4fc8127c_1_f3, l_4bit_sub_beb1027c_1_f0,
       l_4bit_sub_beb1027c_1_f1, l_4bit_sub_beb1027c_1_f2, l_4bit_sub_beb1027c_1_f3,
       l_4bit_xor_4aeb7194_1_f0, l_4bit_xor_4aeb7194_1_f1, l_4bit_xor_4aeb7194_1_f2, l_4bit_xor_4aeb7194_1_f3;

  L_4bit_Adder_fc6744fc l_4bit_adder_fc6744fc_1 (
    .A0(A0), .B0(B0), .A1(A1), .B1(B1), .A2(A2), .B2(B2), .A3(A3), .B3(B3), .F0(l_4bit_adder_fc6744fc_1_f0),
    .F1(l_4bit_adder_fc6744fc_1_f1), .F2(l_4bit_adder_fc6744fc_1_f2), .F3(l_4bit_adder_fc6744fc_1_f3),
    .Cout(Cout));  // open: Cin
  L_4bit_Sub_beb1027c l_4bit_sub_beb1027c_1 (
    .B0(A0), .A0(B0), .B1(A1), .A1(B1), .A2(A2), .B2(B2), .A3(A3), .B3(B3), .F0(l_4bit_sub_beb1027c_1_f0),
    .F1(l_4bit_sub_beb1027c_1_f1), .F2(l_4bit_sub_beb1027c_1_f2), .F3(l_4bit_sub_beb1027c_1_f3));  // open: Cout
  L_4bit_AND_42e6373c l_4bit_and_42e6373c_1 (
    .A0(A0), .B0(B0), .A1(A1), .B1(B1), .A2(A2), .B2(B2), .A3(A3), .B3(B3), .F0(l_4bit_and_42e6373c_1_f0),
    .F1(l_4bit_and_42e6373c_1_f1), .F2(l_4bit_and_42e6373c_1_f2), .F3(l_4bit_and_42e6373c_1_f3));
  L_4bit_OR_4fc8127c l_4bit_or_4fc8127c_1 (
    .A0(A0), .B0(B0), .A1(A1), .B1(B1), .A2(A2), .B2(B2), .A3(A3), .B3(B3), .F0(l_4bit_or_4fc8127c_1_f0),
    .F1(l_4bit_or_4fc8127c_1_f1), .F2(l_4bit_or_4fc8127c_1_f2), .F3(l_4bit_or_4fc8127c_1_f3));
  L_4bit_XOR_4aeb7194 l_4bit_xor_4aeb7194_1 (
    .A0(A0), .B0(B0), .A1(A1), .B1(B1), .A2(A2), .B2(B2), .A3(A3), .B3(B3), .F0(l_4bit_xor_4aeb7194_1_f0),
    .F1(l_4bit_xor_4aeb7194_1_f1), .F2(l_4bit_xor_4aeb7194_1_f2), .F3(l_4bit_xor_4aeb7194_1_f3));
  L_4bit_NOT_d5e80a42 l_4bit_not_d5e80a42_1 (
    .A0(A0), .A1(A1), .A2(A2), .A3(A3), .F0(l_4bit_not_d5e80a42_1_f0), .F1(l_4bit_not_d5e80a42_1_f1),
    .F2(l_4bit_not_d5e80a42_1_f2), .F3(l_4bit_not_d5e80a42_1_f3));
  Multiplexer #(.select(3), .enable("false")) multiplexer_1 (
    .in0(l_4bit_adder_fc6744fc_1_f0), .in1(l_4bit_sub_beb1027c_1_f0), .in2(l_4bit_and_42e6373c_1_f0),
    .in3(l_4bit_or_4fc8127c_1_f0), .in4(l_4bit_xor_4aeb7194_1_f0), .in5(l_4bit_not_d5e80a42_1_f0), .out(F0),
    .sel(Opcode));  // open: in6, in7
  Multiplexer #(.select(3), .enable("false")) multiplexer_2 (
    .in0(l_4bit_adder_fc6744fc_1_f1), .in1(l_4bit_sub_beb1027c_1_f1), .in2(l_4bit_and_42e6373c_1_f1),
    .in3(l_4bit_or_4fc8127c_1_f1), .in4(l_4bit_xor_4aeb7194_1_f1), .in5(l_4bit_not_d5e80a42_1_f1), .out(F1),
    .sel(Opcode));  // open: in6, in7
  Multiplexer #(.select(3), .enable("false")) multiplexer_3 (
    .in0(l_4bit_adder_fc6744fc_1_f2), .in1(l_4bit_sub_beb1027c_1_f2), .in2(l_4bit_and_42e6373c_1_f2),
    .in3(l_4bit_or_4fc8127c_1_f2), .in4(l_4bit_xor_4aeb7194_1_f2), .in5(l_4bit_not_d5e80a42_1_f2), .out(F2),
    .sel(Opcode));  // open: in6, in7
  Multiplexer #(.select(3), .enable("false")) multiplexer_4 (
    .in0(l_4bit_adder_fc6744fc_1_f3), .in1(l_4bit_sub_beb1027c_1_f3), .in2(l_4bit_and_42e6373c_1_f3),
    .in3(l_4bit_or_4fc8127c_1_f3), .in4(l_4bit_xor_4aeb7194_1_f3), .in5(l_4bit_not_d5e80a42_1_f3), .out(F3),
    .sel(Opcode));  // open: in6, in7
endmodule

module L_4bit_computer (
  input  in_1,
  input  in_2
);

  wire and_2_out, button_1_out, Clock, d_ff_1_q, d_ff_2_q, d_ff_3_q, d_ff_4_q, d_ff_5_q, d_ff_6_q, d_ff_10_q,
       d_ff_11_q, decoder_1_out0, decoder_1_out1, decoder_1_out2, decoder_1_out3, decoder_1_out4,
       decoder_1_out5, decoder_1_out6, decoder_1_out7, decoder_1_out8, decoder_1_out9, decoder_1_out10,
       decoder_1_out11, decoder_1_out12, decoder_1_out13, decoder_1_out15,
       l_7_segment_display_driver_7cf2ad60_1_p5, l_7_segment_display_driver_7cf2ad60_1_p6,
       l_7_segment_display_driver_7cf2ad60_1_p7, l_7_segment_display_driver_7cf2ad60_1_p8,
       l_7_segment_display_driver_7cf2ad60_1_p9, l_7_segment_display_driver_7cf2ad60_1_p10,
       l_7_segment_display_driver_7cf2ad60_1_p11, l_7_segment_display_driver_7cf2ad60_2_p2,
       l_7_segment_display_driver_7cf2ad60_2_p8, l_7_segment_display_driver_7cf2ad60_2_p9,
       l_7_segment_display_driver_7cf2ad60_2_p10, l_7_segment_display_driver_7cf2ad60_2_p11,
       l_7_segment_display_driver_7cf2ad60_2_p12, l_7_segment_display_driver_7cf2ad60_2_p13,
       l_7_segment_display_driver_7cf2ad60_2_p14, not_1_out, not_2_out, not_4_out, not_5_out, or_1_out,
       or_2_out, or_3_out, or_6_out, or_7_out, or_8_out, or_9_out, or_11_out, shift_register_1_p1;
  wire [1:0] not_3_out, or_4_out;
  wire [2:0] data_select, demultiplexer_2_out0_2;
  wire [3:0] demultiplexer_1_out0, demultiplexer_1_out1, demultiplexer_1_out2, demultiplexer_1_out3,
       demultiplexer_1_out4, demultiplexer_2_out1, demultiplexer_2_out2, demultiplexer_3_out1,
       dipswitch_1_sw1, l_4bit_alu_eb8587b2_1_f0, multiplexer_1_out, multiplexer_2_out, multiplexer_3_out,
       ram_1_data, ram_2_dout, register_1_q, register_2_q, register_3_q, register_4_q;
  wire [3:3] demultiplexer_2_out0;
  wire [7:0] counter_1_q, shift_register_1_p9;

  Decoder #(.select(4), .enable("false")) decoder_1 (
    .out0(decoder_1_out0), .out1(decoder_1_out1), .out2(decoder_1_out2), .out3(decoder_1_out3),
    .out4(decoder_1_out4), .out5(decoder_1_out5), .out6(decoder_1_out6), .out7(decoder_1_out7),
    .out8(decoder_1_out8), .out9(decoder_1_out9), .out10(decoder_1_out10), .out11(decoder_1_out11),
    .out12(decoder_1_out12), .out13(decoder_1_out13), .out15(decoder_1_out15),
    .sel({demultiplexer_2_out0[3], demultiplexer_2_out0_2}));  // open: out14
  or or_1 (or_1_out, decoder_1_out8, decoder_1_out9, decoder_1_out10, decoder_1_out11, decoder_1_out12, decoder_1_out13);
  D_Flip_Flop d_ff_1 (.D(decoder_1_out15), .clk(Clock), .Q(d_ff_1_q));  // open: Qn, preset, reset
  Register #(.width(4)) register_1 (.D(register_3_q), .en(decoder_1_out6), .clk(Clock), .Q(register_1_q));  // open: clr
  Register #(.width(4)) register_2 (.D(register_3_q), .en(decoder_1_out7), .clk(Clock), .Q(register_2_q));  // open: clr
  or or_2 (or_2_out, decoder_1_out3, decoder_1_out5, decoder_1_out2, decoder_1_out1, decoder_1_out4);
  D_Flip_Flop d_ff_2 (.D(or_2_out), .clk(Clock), .Q(d_ff_2_q));  // open: Qn, preset, reset
  D_Flip_Flop d_ff_3 (.D(decoder_1_out5), .clk(Clock), .Q(d_ff_3_q));  // open: Qn, preset, reset
  D_Flip_Flop d_ff_4 (.D(d_ff_1_q), .clk(Clock), .Q(d_ff_4_q));  // open: Qn, preset, reset
  Button button_1 (.out(button_1_out));
  Counter counter_1 (
    .clr(button_1_out), .load(d_ff_5_q), .up(not_1_out), .clk(Clock), .D(shift_register_1_p9), .Q(counter_1_q));  // open: count, carry
  or or_3 (or_3_out, d_ff_5_q, d_ff_4_q);
  not not_1 (not_1_out, or_3_out);
  Clock clock_1 (.out(Clock));
  D_Flip_Flop d_ff_5 (.D(d_ff_4_q), .clk(Clock), .Q(d_ff_5_q));  // open: Qn, preset, reset
  or or_4 (or_4_out[0], d_ff_2_q, 1'b0);
  or or_5 (or_4_out[1], or_6_out, d_ff_6_q);
  or or_6 (or_6_out, d_ff_1_q, d_ff_4_q, d_ff_5_q);
  D_Flip_Flop d_ff_6 (.D(d_ff_5_q), .clk(Clock), .Q(d_ff_6_q));  // open: Qn, preset, reset
  L_4bit_ALU_eb8587b2 l_4bit_alu_eb8587b2_1 (
    .A0(register_1_q[0]), .B0(register_2_q[0]), .A1(register_1_q[1]), .B1(register_2_q[1]),
    .A2(register_1_q[2]), .B2(register_2_q[2]), .A3(register_1_q[3]), .B3(register_2_q[3]),
    .Opcode(demultiplexer_2_out0_2), .F0(l_4bit_alu_eb8587b2_1_f0[0]), .F1(l_4bit_alu_eb8587b2_1_f0[1]),
    .F2(l_4bit_alu_eb8587b2_1_f0[2]), .F3(l_4bit_alu_eb8587b2_1_f0[3]));  // open: Cout
  Demultiplexer #(.select(3), .width(4), .enable("false")) demultiplexer_1 (
    .out0(demultiplexer_1_out0), .out1(demultiplexer_1_out1), .out2(demultiplexer_1_out2),
    .out3(demultiplexer_1_out3), .out4(demultiplexer_1_out4), .in(demultiplexer_2_out1), .sel(data_select));  // open: out5, out6, out7
  or or_7 (or_7_out, decoder_1_out1, decoder_1_out3);
  or or_8 (or_8_out, decoder_1_out2, decoder_1_out3);
  not not_2 (not_2_out, or_6_out);
  Demultiplexer #(.select(2), .width(4), .enable("false")) demultiplexer_2 (
    .out0({demultiplexer_2_out0[3], demultiplexer_2_out0_2}), .out1(demultiplexer_2_out1),
    .out2(demultiplexer_2_out2), .in(ram_1_data), .sel(or_4_out));  // open: out3
  D_Flip_Flop d_ff_7 (.D(or_7_out), .clk(Clock), .Q(data_select[0]));  // open: Qn, preset, reset
  D_Flip_Flop d_ff_8 (.D(or_8_out), .clk(Clock), .Q(data_select[1]));  // open: Qn, preset, reset
  D_Flip_Flop d_ff_9 (.D(decoder_1_out4), .clk(Clock), .Q(data_select[2]));  // open: Qn, preset, reset
  // Shift_Register #(.width(4), .length(2)) shift_register_1: pin names not known; wires that end beside it: shift_register_1_p1, or_6_out, not_2_out, Clock, demultiplexer_2_out2, shift_register_1_p9[7:4], or_7_out, shift_register_1_p9[7:4], shift_register_1_p9[3:0]
  Multiplexer #(.select(2), .width(4), .enable("false")) multiplexer_1 (
    .in0(l_4bit_alu_eb8587b2_1_f0), .in1(demultiplexer_1_out0), .in2(multiplexer_3_out), .in3(ram_2_dout),
    .out(multiplexer_1_out), .sel(not_3_out));
  or or_9 (or_9_out, not_3_out[1], or_1_out, d_ff_3_q);
  Register #(.width(4)) register_3 (.D(multiplexer_1_out), .en(or_9_out), .clk(Clock), .Q(register_3_q));  // open: clr
  or or_10 (not_3_out[1], d_ff_10_q, d_ff_11_q);
  D_Flip_Flop d_ff_10 (.D(decoder_1_out2), .clk(Clock), .Q(d_ff_10_q));  // open: Qn, preset, reset
  RAM #(.dataWidth(4)) ram_1 (.addr(counter_1_q), .we(in_2), .oe(1'b1), .clk(Clock), .data(ram_1_data));
  or or_11 (or_11_out, or_1_out, d_ff_10_q);
  not not_3 (not_3_out[0], or_11_out);
  not not_4 (not_4_out, d_ff_10_q);
  and and_1 (shift_register_1_p1, not_4_out, data_select[1]);
  Multiplexer #(.width(4), .enable("false")) multiplexer_2 (
    .in0(demultiplexer_1_out3), .in1(demultiplexer_1_out4), .out(multiplexer_2_out), .sel(data_select[2]));
  not not_5 (not_5_out, shift_register_1_p1);
  Multiplexer #(.select(4), .width(4), .enable("false")) multiplexer_3 (
    .in4(dipswitch_1_sw1), .out(multiplexer_3_out), .sel(demultiplexer_1_out2));  // open: in0, in1, in2, in3, in5, in6, in7, in8, in9, in10, in11, in12, in13, in14, in15
  Demultiplexer #(.select(4), .width(4), .enable("false")) demultiplexer_3 (
    .out1(demultiplexer_3_out1), .in(register_3_q), .sel(demultiplexer_1_out1));  // open: out0, out2, out3, out4, out5, out6, out7, out8, out9, out10, out11, out12, out13, out14, out15
  RAM #(.addrWidth(4), .dataWidth(4), .databus("bibus")) ram_2 (
    .addr(multiplexer_2_out), .we(data_select[2]), .oe(d_ff_11_q), .clk(Clock), .din(register_3_q),
    .dout(ram_2_dout));
  Register #(.width(4)) register_4 (
    .D(demultiplexer_3_out1), .en(and_2_out), .clk(Clock), .Q(register_4_q), .clr(in_1));
  and and_2 (and_2_out, not_5_out, data_select[0]);
  D_Flip_Flop d_ff_11 (.D(shift_register_1_p1), .clk(Clock), .Q(d_ff_11_q));  // open: Qn, preset, reset
  DipSwitch #(.number(4)) dipswitch_1 (
    .sw1(dipswitch_1_sw1[0]), .sw2(dipswitch_1_sw1[1]), .sw3(dipswitch_1_sw1[2]), .sw4(dipswitch_1_sw1[3]));
  LED led_1 (.in(register_4_q[0]));
  LED led_2 (.in(register_4_q[1]));
  LED led_3 (.in(register_4_q[2]));
  LED led_4 (.in(register_4_q[3]));
  // L_7_segment_display_driver_7cf2ad60 l_7_segment_display_driver_7cf2ad60_1: pin names not known; wires that end beside it: dipswitch_1_sw1[3], dipswitch_1_sw1[2], dipswitch_1_sw1[1], dipswitch_1_sw1[0], l_7_segment_display_driver_7cf2ad60_1_p5, l_7_segment_display_driver_7cf2ad60_1_p6, l_7_segment_display_driver_7cf2ad60_1_p7, l_7_segment_display_driver_7cf2ad60_1_p8, l_7_segment_display_driver_7cf2ad60_1_p9, l_7_segment_display_driver_7cf2ad60_1_p10, l_7_segment_display_driver_7cf2ad60_1_p11
  _7_Segment_Display u_7_segment_display_1 (
    .g(l_7_segment_display_driver_7cf2ad60_1_p11), .f(l_7_segment_display_driver_7cf2ad60_1_p10),
    .a(l_7_segment_display_driver_7cf2ad60_1_p5), .b(l_7_segment_display_driver_7cf2ad60_1_p6),
    .e(l_7_segment_display_driver_7cf2ad60_1_p9), .d(l_7_segment_display_driver_7cf2ad60_1_p8),
    .c(l_7_segment_display_driver_7cf2ad60_1_p7));  // open: dp
  _7_Segment_Display u_7_segment_display_2 (
    .g(l_7_segment_display_driver_7cf2ad60_2_p14), .f(l_7_segment_display_driver_7cf2ad60_2_p13),
    .a(l_7_segment_display_driver_7cf2ad60_2_p8), .b(l_7_segment_display_driver_7cf2ad60_2_p9),
    .e(l_7_segment_display_driver_7cf2ad60_2_p12), .d(l_7_segment_display_driver_7cf2ad60_2_p11),
    .c(l_7_segment_display_driver_7cf2ad60_2_p10));  // open: dp
  // L_7_segment_display_driver_7cf2ad60 l_7_segment_display_driver_7cf2ad60_2: pin names not known; wires that end beside it: 1'b1, l_7_segment_display_driver_7cf2ad60_2_p2, l_7_segment_display_driver_7cf2ad60_2_p2, register_4_q[3], register_4_q[2], register_4_q[1], register_4_q[0], l_7_segment_display_driver_7cf2ad60_2_p8, l_7_segment_display_driver_7cf2ad60_2_p9, l_7_segment_display_driver_7cf2ad60_2_p10, l_7_segment_display_driver_7cf2ad60_2_p11, l_7_segment_display_driver_7cf2ad60_2_p12, l_7_segment_display_driver_7cf2ad60_2_p13, l_7_segment_display_driver_7cf2ad60_2_p14

  // Notes on the sheet:
  //   reg B
  //   reg C
  //   reg A
  //   Out_LDA
  //   In_LDA
  //   STA
  //   IN
  //   LDA
  //   STA
endmodule

module L_7segment_dec (
);

  Decoder #(.select(4)) decoder_1 ();  // open: out0, out1, out2, out3, out4, out5, out6, out7, out8, out9, out10, out11, out12, out13, out14, out15, sel, en
endmodule
